# Fritzing sketch SchemaConnexion (saved by Fritzing 0.9.5d)

parts:
  Raspberry_Pi_1 = Raspberry Pi 3 [part_number=RPI-3-V1.2]
  S2 = Pushbutton [package="[SMD]"]
  S3 = Pushbutton [package="[SMD]"]
  U1 = TRANSCHIPTC5747 [package=camera_sfv24r-2st_2]  # not connected
  R3 = Resistor [tolerance=±5% resistance=220 package="2512 [SMD]"]
  R4 = Resistor [tolerance=±5% resistance=220 package="2512 [SMD]"]

nets:
  N1: Raspberry_Pi_1.GPIO23, S2.Pin_2
  N2: Raspberry_Pi_1.GND, R3.Pin_1, R4.Pin_1
  N3: Raspberry_Pi_1.GPIO18, S3.Pin_3, S3.Pin_4
  N4: S2.Pin_3, S2.Pin_4, R4.Pin_0
  N5: S3.Pin_1, S3.Pin_2, R3.Pin_0
